// Logisim project 4路组相联cache.circ as structural Verilog: 2 circuits
module \Cache_4路组相联  (
  input  [31:0] BlockDataIn,
  input  [15:0] Addr,
  input  BlkDataReady,
  input  CLK,
  output Miss,
  output [7:0] DataOut
);

  wire and_1_out, comparator_1_eq, comparator_2_eq, comparator_3_eq, comparator_4_eq, d_ff_1_q, d_ff_2_q,
       d_ff_3_q, d_ff_4_q, d_ff_5_q, d_ff_6_q, d_ff_7_q, d_ff_8_q, FULL, Hit, L0, L1, L2, L3, L4, L5, L6, L7,
       multiplexer_7_out, multiplexer_8_out, multiplexer_9_out, multiplexer_10_out, not_1_out, not_2_out,
       not_3_out, not_4_out, not_5_out, not_6_out, not_7_out, not_8_out, v0, v1, v2, v3, v4, v5, v6, v7,
       write0, write1, write2, write3, write4, write5, write6, write7;
  wire [1:0] \max2_归并比较_1_max_num , \max2_归并比较_2_max_num , \max2_归并比较_3_max_num , \max2_归并比较_4_max_num ,
       \max2_归并比较_5_max_num , \max2_归并比较_6_max_num , multiplexer_6_out, out, row;
  wire [12:0] tag0, tag1, tag2, tag3, tag4, tag5, tag6, tag7;
  wire [13:0] multiplexer_2_out, multiplexer_3_out, multiplexer_4_out, multiplexer_5_out;
  wire [15:0] c0, c1, c2, c3, c4, c5, c6, c7, \max2_归并比较_1_max , \max2_归并比较_2_max , \max2_归并比较_3_max ,
       \max2_归并比较_4_max ;
  wire [31:0] register_17_q, register_18_q, register_19_q, register_20_q, register_21_q, register_22_q,
       register_23_q, register_24_q, Slot;

  Register #(.width(1)) register_1 (.D(1'b1), .en(write3), .Q(v3), .clk(CLK));  // open: clr
  Register #(.width(1)) register_2 (.D(1'b1), .en(write4), .Q(v4), .clk(CLK));  // open: clr
  Register #(.width(1)) register_3 (.D(1'b1), .en(write5), .Q(v5), .clk(CLK));  // open: clr
  Register #(.width(1)) register_4 (.D(1'b1), .en(write6), .Q(v6), .clk(CLK));  // open: clr
  Register #(.width(1)) register_5 (.D(1'b1), .en(write7), .Q(v7), .clk(CLK));  // open: clr
  Register #(.width(1)) register_6 (.D(1'b1), .en(write0), .Q(v0), .clk(CLK));  // open: clr
  Register #(.width(1)) register_7 (.D(1'b1), .en(write1), .Q(v1), .clk(CLK));  // open: clr
  Register #(.width(1)) register_8 (.D(1'b1), .en(write2), .Q(v2), .clk(CLK));  // open: clr
  Multiplexer #(.select(2), .width(8), .enable("false")) multiplexer_1 (
    .in0(Slot[7:0]), .in1(Slot[15:8]), .in2(Slot[23:16]), .in3(Slot[31:24]), .out(DataOut), .sel(Addr[1:0]));
  Register #(.width(13)) register_9 (.D(Addr[15:3]), .en(write0), .Q(tag0), .clk(CLK));  // open: clr
  Register #(.width(13)) register_10 (.D(Addr[15:3]), .en(write1), .Q(tag1), .clk(CLK));  // open: clr
  Register #(.width(13)) register_11 (.D(Addr[15:3]), .en(write2), .Q(tag2), .clk(CLK));  // open: clr
  Register #(.width(13)) register_12 (.D(Addr[15:3]), .en(write3), .Q(tag3), .clk(CLK));  // open: clr
  Register #(.width(13)) register_13 (.D(Addr[15:3]), .en(write4), .Q(tag4), .clk(CLK));  // open: clr
  Register #(.width(13)) register_14 (.D(Addr[15:3]), .en(write5), .Q(tag5), .clk(CLK));  // open: clr
  Register #(.width(13)) register_15 (.D(Addr[15:3]), .en(write6), .Q(tag6), .clk(CLK));  // open: clr
  Register #(.width(13)) register_16 (.D(Addr[15:3]), .en(write7), .Q(tag7), .clk(CLK));  // open: clr
  Counter #(.width(16), .max('hffff)) counter_1 (
    .D({16{1'b0}}), .Q(c0), .clk(CLK), .clr(d_ff_1_q));  // open: load, count, carry
  Counter #(.width(16), .max('hffff)) counter_2 (
    .D({16{1'b0}}), .Q(c1), .clk(CLK), .clr(d_ff_2_q));  // open: load, count, carry
  Counter #(.width(16), .max('hffff)) counter_3 (
    .D({16{1'b0}}), .Q(c2), .clk(CLK), .clr(d_ff_3_q));  // open: load, count, carry
  Counter #(.width(16), .max('hffff)) counter_4 (
    .D({16{1'b0}}), .Q(c3), .clk(CLK), .clr(d_ff_4_q));  // open: load, count, carry
  Counter #(.width(16), .max('hffff)) counter_5 (
    .D({16{1'b0}}), .Q(c4), .clk(CLK), .clr(d_ff_5_q));  // open: load, count, carry
  Counter #(.width(16), .max('hffff)) counter_6 (
    .D({16{1'b0}}), .Q(c5), .clk(CLK), .clr(d_ff_6_q));  // open: load, count, carry
  Counter #(.width(16), .max('hffff)) counter_7 (
    .D({16{1'b0}}), .Q(c6), .clk(CLK), .clr(d_ff_7_q));  // open: load, count, carry
  Counter #(.width(16), .max('hffff)) counter_8 (
    .D({16{1'b0}}), .Q(c7), .clk(CLK), .clr(d_ff_8_q));  // open: load, count, carry
  Register #(.width(32)) register_17 (.D(BlockDataIn), .en(write0), .Q(register_17_q), .clk(CLK));  // open: clr
  Register #(.width(32)) register_18 (.D(BlockDataIn), .en(write1), .Q(register_18_q), .clk(CLK));  // open: clr
  Register #(.width(32)) register_19 (.D(BlockDataIn), .en(write2), .Q(register_19_q), .clk(CLK));  // open: clr
  Register #(.width(32)) register_20 (.D(BlockDataIn), .en(write3), .Q(register_20_q), .clk(CLK));  // open: clr
  Register #(.width(32)) register_21 (.D(BlockDataIn), .en(write4), .Q(register_21_q), .clk(CLK));  // open: clr
  Register #(.width(32)) register_22 (.D(BlockDataIn), .en(write5), .Q(register_22_q), .clk(CLK));  // open: clr
  Register #(.width(32)) register_23 (.D(BlockDataIn), .en(write6), .Q(register_23_q), .clk(CLK));  // open: clr
  Register #(.width(32)) register_24 (.D(BlockDataIn), .en(write7), .Q(register_24_q), .clk(CLK));  // open: clr
  D_Flip_Flop d_ff_1 (.clk(CLK), .D(L0), .Q(d_ff_1_q));  // open: Qn, preset, en, reset
  assign Slot = L0 ? register_17_q : 32'bz;  // Controlled_Buffer controlled_buffer_1
  D_Flip_Flop d_ff_2 (.clk(CLK), .D(L1), .Q(d_ff_2_q));  // open: Qn, preset, en, reset
  assign Slot = L1 ? register_18_q : 32'bz;  // Controlled_Buffer controlled_buffer_2
  D_Flip_Flop d_ff_3 (.clk(CLK), .D(L2), .Q(d_ff_3_q));  // open: Qn, preset, en, reset
  assign Slot = L2 ? register_19_q : 32'bz;  // Controlled_Buffer controlled_buffer_3
  D_Flip_Flop d_ff_4 (.clk(CLK), .D(L3), .Q(d_ff_4_q));  // open: Qn, preset, en, reset
  assign Slot = L3 ? register_20_q : 32'bz;  // Controlled_Buffer controlled_buffer_4
  D_Flip_Flop d_ff_5 (.clk(CLK), .D(L4), .Q(d_ff_5_q));  // open: Qn, preset, en, reset
  assign Slot = L4 ? register_21_q : 32'bz;  // Controlled_Buffer controlled_buffer_5
  D_Flip_Flop d_ff_6 (.clk(CLK), .D(L5), .Q(d_ff_6_q));  // open: Qn, preset, en, reset
  assign Slot = L5 ? register_22_q : 32'bz;  // Controlled_Buffer controlled_buffer_6
  D_Flip_Flop d_ff_7 (.clk(CLK), .D(L6), .Q(d_ff_7_q));  // open: Qn, preset, en, reset
  assign Slot = L6 ? register_23_q : 32'bz;  // Controlled_Buffer controlled_buffer_7
  D_Flip_Flop d_ff_8 (.clk(CLK), .D(L7), .Q(d_ff_8_q));  // open: Qn, preset, en, reset
  assign Slot = L7 ? register_24_q : 32'bz;  // Controlled_Buffer controlled_buffer_8
  not not_1 (not_1_out, v0);
  not not_2 (not_2_out, v4);
  not not_3 (not_3_out, v1);
  not not_4 (not_4_out, v5);
  not not_5 (not_5_out, v2);
  not not_6 (not_6_out, v6);
  not not_7 (not_7_out, v3);
  not not_8 (not_8_out, v7);
  // Probe on multiplexer_2_out
  Multiplexer #(.width(14), .enable("false")) multiplexer_2 (
    .in0({v2, tag2}), .in1({v6, tag6}), .out(multiplexer_2_out), .sel(Addr[2]));
  // Probe on multiplexer_3_out
  Multiplexer #(.width(14), .enable("false")) multiplexer_3 (
    .in0({v1, tag1}), .in1({v5, tag5}), .out(multiplexer_3_out), .sel(Addr[2]));
  // Probe on multiplexer_4_out
  Multiplexer #(.width(14), .enable("false")) multiplexer_4 (
    .in0({v3, tag3}), .in1({v7, tag7}), .out(multiplexer_4_out), .sel(Addr[2]));
  // Probe on multiplexer_5_out
  Multiplexer #(.width(14), .enable("false")) multiplexer_5 (
    .in0({v0, tag0}), .in1({v4, tag4}), .out(multiplexer_5_out), .sel(Addr[2]));
  and and_1 (and_1_out, BlkDataReady, Miss);
  Demultiplexer #(.select(3), .enable("false")) demultiplexer_1 (
    .out0(write0), .out1(write1), .out2(write2), .out3(write3), .out4(write4), .out5(write5), .out6(write6),
    .out7(write7), .in(and_1_out), .sel({Addr[2], multiplexer_6_out}));
  Multiplexer #(.width(2), .enable("false")) multiplexer_6 (.in0(row), .in1(out), .out(multiplexer_6_out), .sel(FULL));
  Multiplexer #(.enable("false")) multiplexer_7 (
    .in0(not_1_out), .in1(not_2_out), .out(multiplexer_7_out), .sel(Addr[2]));
  Multiplexer #(.enable("false")) multiplexer_8 (
    .in0(not_3_out), .in1(not_4_out), .out(multiplexer_8_out), .sel(Addr[2]));
  Multiplexer #(.enable("false")) multiplexer_9 (
    .in0(not_5_out), .in1(not_6_out), .out(multiplexer_9_out), .sel(Addr[2]));
  Multiplexer #(.enable("false")) multiplexer_10 (
    .in0(not_7_out), .in1(not_8_out), .out(multiplexer_10_out), .sel(Addr[2]));
  \Max2_归并比较  \max2_归并比较_1  (
    .Y(c1), .X(c0), .Y_num(2'b01), .X_num(2'b00), .MAX(\max2_归并比较_1_max ), .MAX_num(\max2_归并比较_1_max_num ));
  \Max2_归并比较  \max2_归并比较_2  (
    .Y(c3), .X(c2), .Y_num(2'b11), .X_num(2'b10), .MAX(\max2_归并比较_2_max ), .MAX_num(\max2_归并比较_2_max_num ));
  \Max2_归并比较  \max2_归并比较_3  (
    .Y(c5), .X(c4), .Y_num(2'b01), .X_num(2'b00), .MAX(\max2_归并比较_3_max ), .MAX_num(\max2_归并比较_3_max_num ));
  \Max2_归并比较  \max2_归并比较_4  (
    .Y(c7), .X(c6), .Y_num(2'b11), .X_num(2'b10), .MAX(\max2_归并比较_4_max ), .MAX_num(\max2_归并比较_4_max_num ));
  Comparator #(.width(14)) comparator_1 (
    .a(multiplexer_2_out), .b({1'b1, Addr[15:3]}), .eq(comparator_1_eq));  // open: gt, lt
  Comparator #(.width(14)) comparator_2 (
    .a(multiplexer_3_out), .b({1'b1, Addr[15:3]}), .eq(comparator_2_eq));  // open: gt, lt
  Comparator #(.width(14)) comparator_3 (
    .a(multiplexer_4_out), .b({1'b1, Addr[15:3]}), .eq(comparator_3_eq));  // open: gt, lt
  Comparator #(.width(14)) comparator_4 (
    .a(multiplexer_5_out), .b({1'b1, Addr[15:3]}), .eq(comparator_4_eq));  // open: gt, lt
  Priority_Encoder #(.select(2)) priority_encoder_1 (
    .in0(multiplexer_7_out), .in1(multiplexer_8_out), .in2(multiplexer_9_out), .in3(multiplexer_10_out),
    .out(row), .en_out(FULL), .en_in(1'b1));  // open: gs
  \Max2_归并比较  \max2_归并比较_5  (
    .Y(\max2_归并比较_2_max ), .X(\max2_归并比较_1_max ), .Y_num(\max2_归并比较_2_max_num ),
    .X_num(\max2_归并比较_1_max_num ), .MAX_num(\max2_归并比较_5_max_num ));  // open: MAX
  Multiplexer #(.width(2), .enable("false")) multiplexer_11 (
    .in0(\max2_归并比较_5_max_num ), .in1(\max2_归并比较_6_max_num ), .out(out), .sel(Addr[2]));
  \Max2_归并比较  \max2_归并比较_6  (
    .Y(\max2_归并比较_4_max ), .X(\max2_归并比较_3_max ), .Y_num(\max2_归并比较_4_max_num ),
    .X_num(\max2_归并比较_3_max_num ), .MAX_num(\max2_归并比较_6_max_num ));  // open: MAX
  Demultiplexer #(.enable("false")) demultiplexer_2 (.out0(L2), .out1(L6), .in(comparator_1_eq), .sel(Addr[2]));
  Demultiplexer #(.enable("false")) demultiplexer_3 (.out0(L1), .out1(L5), .in(comparator_2_eq), .sel(Addr[2]));
  Demultiplexer #(.enable("false")) demultiplexer_4 (.out0(L3), .out1(L7), .in(comparator_3_eq), .sel(Addr[2]));
  Demultiplexer #(.enable("false")) demultiplexer_5 (.out0(L0), .out1(L4), .in(comparator_4_eq), .sel(Addr[2]));
  // Probe on row
  not not_9 (Miss, Hit);
  or or_1 (Hit, comparator_1_eq, comparator_2_eq, comparator_3_eq, comparator_4_eq);

  // Other names for the same wires on the sheet: tag[12:0] = Addr[15:3]; 字节地址[15:0] = Addr; index = Addr[2];
  //   Blk[31:0] = BlockDataIn; BlkReady = BlkDataReady; offset[1:0] = Addr[1:0]

  // Notes on the sheet:
  //   输入引脚区
  //   请勿增改引脚，请勿修改子电路封装
  //   16位
  //   电路功能：利用上面给定的隧道构建8行的Cache，cache映射方式自选
  //   请在下方利用上方输入输出引脚的隧道信号构建电路，ctrl+d复制选择部件
  //   输出引脚区
endmodule

// Max2
module \Max2_归并比较  (
  input  [15:0] Y,
  input  [15:0] X,
  input  [1:0] Y_num,
  input  [1:0] X_num,
  output [15:0] MAX,
  output [1:0] MAX_num
);

  wire comparator_1_eq, comparator_1_gt, or_1_out;

  Multiplexer #(.width(16)) multiplexer_1 (.in0(Y), .in1(X), .out(MAX), .sel(or_1_out), .en(1'b1));
  Comparator #(.width(16), .mode("unsigned")) comparator_1 (
    .a(X), .b(Y), .gt(comparator_1_gt), .eq(comparator_1_eq));  // open: lt
  or or_1 (or_1_out, comparator_1_gt, comparator_1_eq);
  Multiplexer #(.width(2), .enable("false")) multiplexer_2 (.in0(Y_num), .in1(X_num), .out(MAX_num), .sel(or_1_out));

  // Notes on the sheet:
  //   输出两个输入中的较大值，并输出较大值的2位编号
endmodule
